// Logisim project ECEN240_Final_Project_4bit_CPU.circ as structural Verilog: 6 circuits, main circuit Final_Project
module Final_Project (
  input  CLR
);

  wire CLK, DWE, Sub, WE;
  wire [1:0] AFS, RSS;
  wire [2:0] AddrA, AddrB, AddrD;
  wire [3:0] mux4to1_4bit_1_p3, mux4to1_4bit_1_p5, Opcode;
  wire [3:3] Data;
  wire [7:0] counter_1_q, register_file_3port_1_portb;
  wire [11:7] rom_1_data;

  Counter counter_1 (.clr(CLR), .clk(CLK), .Q(counter_1_q));  // open: load, up, count, D, carry
  Clock u_CLK (.out(CLK));
  // MUX4to1_4bit mux4to1_4bit_1: pin names not known; wires that end beside it: {Data[3], AddrB}, register_file_3port_1_portb[7:4], mux4to1_4bit_1_p3, RSS, mux4to1_4bit_1_p5
  // Probe on mux4to1_4bit_1_p5
  ROM #(.dataWidth(16)) rom_1 (
    .addr(counter_1_q), .data({Opcode, rom_1_data[11], AddrD, rom_1_data[7], AddrA, Data[3], AddrB}));
  ROM #(.addrWidth(4), .dataWidth(7)) rom_2 (.addr(Opcode), .data({Sub, AFS, RSS, DWE, WE}));
  // Probe on {Opcode, rom_1_data[11], AddrD, rom_1_data[7], AddrA, Data[3], AddrB}
  // Probe on register_file_3port_1_portb[7:4]
  Register_File_3Port register_file_3port_1 (
    .RAddrA(AddrA), .RAddrB(AddrB), .WE(WE), .WAddr(AddrD), .Data_in(mux4to1_4bit_1_p5), .Clk(CLK),
    .PortA(register_file_3port_1_portb[7:4]), .PortB(register_file_3port_1_portb[3:0]));
  // Probe on {Data[3], AddrB}
  // Probe on AddrB
  // Probe on register_file_3port_1_portb[3:0]
  // Probe on AddrA
  // Probe on AddrD
  // Probe on Opcode
  // Probe on Sub
  // Probe on DWE
  // Probe on WE
  // Probe on AFS
  // Probe on RSS
  // Probe on register_file_3port_1_portb
  TTY tty_1 (.data(register_file_3port_1_portb[6:0]), .clk(CLK), .we(DWE), .clr(1'b0));
  // Probe on mux4to1_4bit_1_p3
  Sub_ALU sub_alu_1 (
    .A(register_file_3port_1_portb[7:4]), .B(register_file_3port_1_portb[3:0]), .Sub(Sub), .S(AFS),
    .ALU_out(mux4to1_4bit_1_p3));

  // Other names for the same wires on the sheet: Data[2:0] = AddrB

  // Notes on the sheet:
  //   contents of rom_1 (hex, n*v repeats v):
  //   1003 2700 1004 1109 3001 1007 1103 3001 1102 3001 1006 1101 3001 1105 3001 110c 3001 1002 1100 3001
  //   1004 110c 3001 1007 1105 3001 1006 110e 3001 1103 3001 1105 3001 1106 3001 110f 3001 1007 1102 3001
  //   1006 1104 3001 1002 1100 3001 1103 3001 1003 1106 3001 1107 3001 1002 1100 3001 1003 1105 3001 1002
  //   110b 3001 1003 1103 3001 110d 3001 1205 1303 7423 3074 1002 1100 3001 1003 1105 1703 3001 1002 110d
  //   3001 1003 1103 3001 110d 3001 1205 1303 140f 1501 4634 7665 7426 3034 1003 1105 3001 1002 110d 3001
  //   1003 1103 3001 110d 3001 1205 1303 f423 3074 1002 1100 3001 1004 1103 3001 1006 110f 3001 1007 1100
  //   3001 1109 3001 1003 110a 3001 1002 1100 3001 2640 1703 3076
  //   contents of rom_2 (hex, n*v repeats v):
  //   0 1 9 2 5 15 25 35 7*0 75
endmodule

module Register_File_3Port (
  input  [2:0] RAddrA,
  input  [2:0] RAddrB,
  input  WE,
  input  [2:0] WAddr,
  input  [3:0] Data_in,
  input  Clk,
  output [3:0] PortA,
  output [3:0] PortB
);

  wire decoder_1_out0, decoder_1_out1, decoder_1_out2, decoder_1_out3, decoder_1_out4, decoder_1_out5,
       decoder_1_out6, decoder_1_out7;
  wire [3:0] register_four_bits_1_dout, register_four_bits_2_dout, register_four_bits_3_dout,
       register_four_bits_4_dout, register_four_bits_5_dout, register_four_bits_6_dout,
       register_four_bits_7_dout, register_four_bits_8_dout;

  Decoder #(.select(3)) decoder_1 (
    .out0(decoder_1_out0), .out1(decoder_1_out1), .out2(decoder_1_out2), .out3(decoder_1_out3),
    .out4(decoder_1_out4), .out5(decoder_1_out5), .out6(decoder_1_out6), .out7(decoder_1_out7), .sel(WAddr),
    .en(WE));
  Register_Four_Bits register_four_bits_1 (
    .Din(Data_in), .Write(decoder_1_out0), .Clk(Clk), .Dout(register_four_bits_1_dout));
  Register_Four_Bits register_four_bits_2 (
    .Din(Data_in), .Write(decoder_1_out1), .Clk(Clk), .Dout(register_four_bits_2_dout));
  Register_Four_Bits register_four_bits_3 (
    .Din(Data_in), .Write(decoder_1_out2), .Clk(Clk), .Dout(register_four_bits_3_dout));
  Register_Four_Bits register_four_bits_4 (
    .Din(Data_in), .Write(decoder_1_out3), .Clk(Clk), .Dout(register_four_bits_4_dout));
  Register_Four_Bits register_four_bits_5 (
    .Din(Data_in), .Write(decoder_1_out4), .Clk(Clk), .Dout(register_four_bits_5_dout));
  Register_Four_Bits register_four_bits_6 (
    .Din(Data_in), .Write(decoder_1_out5), .Clk(Clk), .Dout(register_four_bits_6_dout));
  Register_Four_Bits register_four_bits_7 (
    .Din(Data_in), .Write(decoder_1_out6), .Clk(Clk), .Dout(register_four_bits_7_dout));
  Register_Four_Bits register_four_bits_8 (
    .Din(Data_in), .Write(decoder_1_out7), .Clk(Clk), .Dout(register_four_bits_8_dout));
  Multiplexer #(.select(3), .width(4)) multiplexer_1 (
    .in0(register_four_bits_1_dout), .in1(register_four_bits_2_dout), .in2(register_four_bits_3_dout),
    .in3(register_four_bits_4_dout), .in4(register_four_bits_5_dout), .in5(register_four_bits_6_dout),
    .in6(register_four_bits_7_dout), .in7(register_four_bits_8_dout), .out(PortA), .sel(RAddrA));
  Multiplexer #(.select(3), .width(4)) multiplexer_2 (
    .in0(register_four_bits_1_dout), .in1(register_four_bits_2_dout), .in2(register_four_bits_3_dout),
    .in3(register_four_bits_4_dout), .in4(register_four_bits_5_dout), .in5(register_four_bits_6_dout),
    .in6(register_four_bits_7_dout), .in7(register_four_bits_8_dout), .out(PortB), .sel(RAddrB));

  // Notes on the sheet:
  //   Israel Lunceford
endmodule

module Register_Four_Bits (
  input  [3:0] Din,
  input  Write,
  input  Clk,
  output [3:0] Dout
);

  wire multiplexer_1_out, multiplexer_2_out, multiplexer_3_out, multiplexer_4_out;

  Multiplexer multiplexer_1 (.in0(Dout[0]), .in1(Din[0]), .out(multiplexer_1_out), .sel(Write));
  Multiplexer multiplexer_2 (.in0(Dout[1]), .in1(Din[1]), .out(multiplexer_2_out), .sel(Write));
  Multiplexer multiplexer_3 (.in0(Dout[2]), .in1(Din[2]), .out(multiplexer_3_out), .sel(Write));
  Multiplexer multiplexer_4 (.in0(Dout[3]), .in1(Din[3]), .out(multiplexer_4_out), .sel(Write));
  D_Flip_Flop d_ff_1 (.D(multiplexer_1_out), .clk(Clk), .Q(Dout[0]));  // open: Qn, preset, reset
  D_Flip_Flop d_ff_2 (.D(multiplexer_2_out), .clk(Clk), .Q(Dout[1]));  // open: Qn, preset, reset
  D_Flip_Flop d_ff_3 (.D(multiplexer_3_out), .clk(Clk), .Q(Dout[2]));  // open: Qn, preset, reset
  D_Flip_Flop d_ff_4 (.D(multiplexer_4_out), .clk(Clk), .Q(Dout[3]));  // open: Qn, preset, reset

  // Notes on the sheet:
  //   Israel Lunceford
endmodule

module Sub_ALU (
  input  [3:0] A,
  input  [3:0] B,
  input  Sub,
  input  [1:0] S,
  output [3:0] ALU_out
);

  wire and_4bit_1_p3, or_4bit_1_p3, xor_4bit_1_p3;
  wire [3:0] or_4bit_1_p6;

  // XOR_4bit xor_4bit_1: pin names not known; wires that end beside it: A, B, xor_4bit_1_p3
  // AND_4bit and_4bit_1: pin names not known; wires that end beside it: A, B, and_4bit_1_p3, xor_4bit_1_p3
  // OR_4bit or_4bit_1: pin names not known; wires that end beside it: A, B, or_4bit_1_p3, or_4bit_1_p3, and_4bit_1_p3, or_4bit_1_p6, S
  Add_Sub_4bit add_sub_4bit_1 (.A(A), .B(B), .Sub(Sub), .Result(or_4bit_1_p6));
  // MUX4to1_4bit mux4to1_4bit_1: pin names not known; wires that end beside it: ALU_out

  // Notes on the sheet:
  //   Israel Lunceford
endmodule

module Add_Sub_4bit (
  input  [3:0] A,
  input  [3:0] B,
  input  Sub,
  output [3:0] Result
);

  wire f_adder_1_cout, f_adder_2_cout, f_adder_3_cout, xor_1_out, xor_2_out, xor_3_out, xor_4_out;

  xor xor_1 (xor_1_out, B[0], Sub);
  xor xor_2 (xor_2_out, B[1], Sub);
  xor xor_3 (xor_3_out, B[2], Sub);
  xor xor_4 (xor_4_out, B[3], Sub);
  F_Adder f_adder_1 (.A(A[0]), .B(xor_1_out), .Cin(Sub), .S(Result[0]), .Cout(f_adder_1_cout));
  F_Adder f_adder_2 (.A(A[1]), .B(xor_2_out), .Cin(f_adder_1_cout), .S(Result[1]), .Cout(f_adder_2_cout));
  F_Adder f_adder_3 (.A(A[2]), .B(xor_3_out), .Cin(f_adder_2_cout), .S(Result[2]), .Cout(f_adder_3_cout));
  F_Adder f_adder_4 (.A(A[3]), .B(xor_4_out), .Cin(f_adder_3_cout), .S(Result[3]));  // open: Cout
endmodule

module F_Adder (
  input  A,
  input  B,
  input  Cin,
  output S,
  output Cout
);

  wire and_1_out, and_2_out, and_3_out, xor_1_out;

  and and_1 (and_1_out, A, B);
  and and_2 (and_2_out, B, Cin);
  and and_3 (and_3_out, A, Cin);
  or or_1 (Cout, and_1_out, and_2_out, and_3_out);
  xor xor_1 (xor_1_out, A, B);
  xor xor_2 (S, xor_1_out, Cin);
endmodule
